// Logisim project cpu.circ as structural Verilog: 6 circuits, main circuit main
// CPU
module main (
  input  [31:0] RS_READ_VALUE,
  input  [31:0] RI_READ_VALUE,
  input  [31:0] RD_READ_VALUE,
  input  [31:0] JC_READ_VALUE,
  input  [31:0] INSTRUCTION,
  input  CLOCK,
  output [4:0] RS,
  output [4:0] RI,
  output [4:0] RD,
  output [31:0] RD_WRITE_VALUE,
  output RD_WRITE_ENABLE,
  output [23:0] FETCH_ADDRESS
);

  wire and_1_out, comparator_5_eq, comparator_5_lt, comparator_6_gt, comparator_6_lt, comparator_7_eq,
       comparator_7_gt, comparator_8_eq, comparator_9_eq, comparator_9_lt, cond1, cond2, cond3, cond4, cond5,
       cond6, I, Jend, Jtype, not_1_out, not_2_out, not_3_out, not_4_out, not_5_out, not_6_out, or_1_out,
       Rtype;
  wire [2:0] JC_t;
  wire [4:0] multiplexer_10_out, RD_t_t;
  wire [16:0] IMM;
  wire [16:5] Rreg;
  wire [23:0] ADDR, bit_extender_1_out, bit_extender_2_out, bit_extender_3_out, bit_extender_4_out,
       bit_extender_5_out, bit_extender_6_out, bit_extender_7_out, bit_extender_8_out, multiplexer_1_out,
       multiplexer_2_out, multiplexer_3_out, multiplexer_4_out, multiplexer_5_out, multiplexer_6_out,
       multiplexer_7_out, multiplexer_8_out, multiplexer_9_out, operation, PC_1;
  wire [23:5] Jreg;
  wire [24:0] bit_extender_11_out;
  wire [31:0] bit_extender_9_out, bit_extender_10_out, dataOut, multiplexer_14_out, multiplexer_15_out,
       result_add;
  wire [31:28] Jim;

  Register #(.width(24)) PCreg (.D(multiplexer_1_out), .Q(FETCH_ADDRESS), .clk(CLOCK));  // open: en, clr
  Bit_Extender #(.in_width(32), .out_width(24)) bit_extender_1 (.in(RI_READ_VALUE), .out(bit_extender_1_out));
  Bit_Extender #(.in_width(32), .out_width(24)) bit_extender_2 (.in(RI_READ_VALUE), .out(bit_extender_2_out));
  Bit_Extender #(.in_width(32), .out_width(24)) bit_extender_3 (.in(RI_READ_VALUE), .out(bit_extender_3_out));
  Bit_Extender #(.in_width(32), .out_width(24)) bit_extender_4 (.in(RI_READ_VALUE), .out(bit_extender_4_out));
  Multiplexer #(.width(24)) multiplexer_1 (
    .in0(multiplexer_8_out), .in1(PC_1), .out(multiplexer_1_out), .sel(or_1_out));  // open: en
  Multiplexer #(.width(24)) multiplexer_2 (
    .in0(bit_extender_1_out), .in1(ADDR), .out(multiplexer_2_out), .sel(I), .en(cond1));
  Multiplexer #(.width(24)) multiplexer_3 (
    .in0(bit_extender_2_out), .in1(ADDR), .out(multiplexer_3_out), .sel(I), .en(cond2));
  Multiplexer #(.width(24)) multiplexer_4 (
    .in0(bit_extender_3_out), .in1(ADDR), .out(multiplexer_4_out), .sel(I), .en(cond3));
  Multiplexer #(.width(24)) multiplexer_5 (
    .in0(bit_extender_4_out), .in1(ADDR), .out(multiplexer_5_out), .sel(I), .en(cond4));
  Bit_Extender #(.in_width(32), .out_width(24)) bit_extender_5 (.in(RI_READ_VALUE), .out(bit_extender_5_out));
  Bit_Extender #(.in_width(32), .out_width(24)) bit_extender_6 (.in(RI_READ_VALUE), .out(bit_extender_6_out));
  or or_1 (or_1_out, Jend, Rtype);
  Multiplexer #(.width(24)) multiplexer_6 (
    .in0(bit_extender_5_out), .in1(ADDR), .out(multiplexer_6_out), .sel(I), .en(cond5));
  Multiplexer #(.width(24)) multiplexer_7 (
    .in0(bit_extender_6_out), .in1(ADDR), .out(multiplexer_7_out), .sel(I), .en(cond6));
  Multiplexer #(.select(3), .width(24)) multiplexer_8 (
    .in0(operation), .in1(multiplexer_2_out), .in2(multiplexer_3_out), .in3(multiplexer_4_out),
    .in4(multiplexer_5_out), .in5(multiplexer_6_out), .in6(multiplexer_7_out), .in7(multiplexer_9_out),
    .out(multiplexer_8_out), .sel(JC_t));  // open: en
  Adder #(.width(24)) adder_1 (.a(FETCH_ADDRESS), .b(24'h1), .out(PC_1));  // open: cin, cout
  Bit_Extender #(.in_width(32), .out_width(24)) bit_extender_7 (.in(RI_READ_VALUE), .out(bit_extender_7_out));
  Multiplexer #(.width(24)) multiplexer_9 (
    .in0(bit_extender_7_out), .in1(ADDR), .out(multiplexer_9_out), .sel(I));  // open: en
  not not_1 (not_1_out, cond1);
  not not_2 (not_2_out, cond2);
  not not_3 (not_3_out, cond3);
  not not_4 (not_4_out, cond4);
  not not_5 (not_5_out, cond5);
  not not_6 (not_6_out, cond6);
  Multiplexer #(.select(3), .width(5)) multiplexer_10 (
    .in7(5'b00110), .out(multiplexer_10_out), .sel(JC_t));  // open: in0, in1, in2, in3, in4, in5, in6, en
  Bit_Extender #(.in_width(32), .out_width(24)) bit_extender_8 (.in(RI_READ_VALUE), .out(bit_extender_8_out));
  Multiplexer #(.select(4), .width(5)) multiplexer_11 (
    .in0(RD_t_t), .in1(RD_t_t), .in2(RD_t_t), .in3(RD_t_t), .in4(RD_t_t), .in5(RD_t_t), .in6(RD_t_t),
    .in7(RD_t_t), .in8(RD_t_t), .in9(RD_t_t), .in10(RD_t_t), .in11(RD_t_t), .in12(RD_t_t), .in13(RD_t_t),
    .in14(RD_t_t), .in15(multiplexer_10_out), .out(RD), .sel(Jim));  // open: en
  Multiplexer #(.width(24)) multiplexer_12 (
    .in0(bit_extender_8_out), .in1(ADDR), .out(operation), .sel(I));  // open: en
  Multiplexer #(.select(3)) multiplexer_13 (
    .in0(1'b0), .in1(not_1_out), .in2(not_2_out), .in3(not_3_out), .in4(not_4_out), .in5(not_5_out),
    .in6(not_6_out), .in7(1'b0), .out(Jend), .sel(JC_t));  // open: en
  Comparator #(.width(4), .mode("unsigned")) comparator_1 (
    .a(INSTRUCTION[31:28]), .b(4'b1111), .eq(Jtype), .lt(Rtype));  // open: gt
  Demultiplexer #(.width(32), .tristate("true")) demultiplexer_1 (
    .out0({Jim, I, RD_t_t, RS, Rreg, RI}), .out1({Jim, I, RD_t_t, RS, IMM}), .in(INSTRUCTION),
    .sel(INSTRUCTION[27]), .en(Rtype));
  assign bit_extender_9_out = {{8{1'b0}}, PC_1};  // Bit_Extender bit_extender_9
  assign bit_extender_10_out = {{15{IMM[16]}}, IMM};  // Bit_Extender bit_extender_10
  Multiplexer #(.select(3), .width(32)) multiplexer_14 (
    .in7(bit_extender_9_out), .out(multiplexer_14_out), .sel(JC_t));  // open: in0, in1, in2, in3, in4, in5, in6, en
  Multiplexer #(.width(32)) multiplexer_15 (
    .in0(RI_READ_VALUE), .in1(bit_extender_10_out), .out(multiplexer_15_out), .sel(I));  // open: en
  Multiplexer #(.select(4), .width(32)) multiplexer_16 (
    .in0(result_add), .in1(result_add), .in2(result_add), .in3(result_add), .in4(result_add),
    .in5(result_add), .in6(result_add), .in7(result_add), .in8(result_add), .in9(result_add), .in10(dataOut),
    .in11(RD_READ_VALUE), .in12(dataOut), .in13(RD_READ_VALUE), .in14(result_add), .in15(multiplexer_14_out),
    .out(RD_WRITE_VALUE), .sel(Jim), .en(RD_WRITE_ENABLE));
  u_ALU u_alu_1 (.ALU_X(RS_READ_VALUE), .ALU_Y(multiplexer_15_out), .ALU_CONTROL(Jim), .ALU_RESULT(result_add));
  Demultiplexer #(.width(32), .tristate("true")) demultiplexer_2 (
    .out0({Jim, I, JC_t, Jreg, RI}), .out1({Jim, I, JC_t, ADDR}), .in(INSTRUCTION), .sel(INSTRUCTION[27]),
    .en(Jtype));
  Comparator #(.width(32)) comparator_2 (.a(JC_READ_VALUE), .b({32{1'b0}}), .gt(cond1));  // open: eq, lt
  Comparator #(.width(32)) comparator_3 (.a(JC_READ_VALUE), .b({32{1'b0}}), .eq(cond2));  // open: gt, lt
  Comparator #(.width(32)) comparator_4 (.a(JC_READ_VALUE), .b({32{1'b0}}), .lt(cond3));  // open: gt, eq
  Comparator #(.width(32)) comparator_5 (
    .a(JC_READ_VALUE), .b({32{1'b0}}), .eq(comparator_5_eq), .lt(comparator_5_lt));  // open: gt
  Comparator #(.width(32)) comparator_6 (
    .a(JC_READ_VALUE), .b({32{1'b0}}), .gt(comparator_6_gt), .lt(comparator_6_lt));  // open: eq
  Comparator #(.width(32)) comparator_7 (
    .a(JC_READ_VALUE), .b({32{1'b0}}), .gt(comparator_7_gt), .eq(comparator_7_eq));  // open: lt
  or or_2 (cond4, comparator_5_eq, comparator_5_lt);
  or or_3 (cond5, comparator_6_gt, comparator_6_lt);
  or or_4 (cond6, comparator_7_gt, comparator_7_eq);
  Bit_Extender #(.in_width(32), .out_width(25), .\type ("sign")) bit_extender_11 (
    .in(result_add), .out(bit_extender_11_out));
  Comparator #(.width(3), .mode("unsigned")) comparator_8 (.a(JC_t), .b(3'b111), .eq(comparator_8_eq));  // open: gt, lt
  Comparator #(.width(4), .mode("unsigned")) comparator_9 (
    .a(Jim), .b(4'b1111), .eq(comparator_9_eq), .lt(comparator_9_lt));  // open: gt
  u_MEM u_mem_1 (
    .ADDRESS(bit_extender_11_out), .WORD_MODE(Jim[30]), .MEM_WRITE(Jim[28]), .DATA_IN(RD_READ_VALUE),
    .CLOCK(CLOCK), .DATA_OUT(dataOut));
  and and_1 (and_1_out, comparator_8_eq, comparator_9_eq);
  or or_5 (RD_WRITE_ENABLE, and_1_out, comparator_9_lt);

  // Other names for the same wires on the sheet: clk = CLOCK; instr[31:0] = INSTRUCTION; JC[31:0] = JC_READ_VALUE;
  //   Jim[27:0] = {I, JC_t, ADDR}; Jreg (some bits) = {Jim, I, JC_t, RI}; Rim[31:0] = {Jim, I, RD_t_t, RS, IMM};
  //   Rreg (some bits) = {Jim, I, RD_t_t, RS, RI}; OP[3:0] = Jim; PC[23:0] = FETCH_ADDRESS;
  //   RD_t[31:0] = RD_READ_VALUE; RD_write[31:0] = RD_WRITE_VALUE; RDselect[4:0] = RD; RI_t[31:0] = RI_READ_VALUE;
  //   RS_t[31:0] = RS_READ_VALUE; Write_enable = RD_WRITE_ENABLE
endmodule

module u_ALU (
  input  [31:0] ALU_X,
  input  [31:0] ALU_Y,
  input  [3:0] ALU_CONTROL,
  output [31:0] ALU_RESULT
);

  wire [4:0] bit_extender_1_out, bit_extender_2_out, bit_extender_3_out;
  wire [31:0] ADD_OUTPUT, AND_OUTPUT, DIV_OUTPUT, LEFT_SHIFT_OUTPUT, MUL_OUTPUT, negator_1_out, OR_OUTPUT,
       REVER_OUTPUT, RIGHT_SHIFT_OUTPUT, RL_S, SUB_OUTPUT, XOR_OUTPUT;

  Bit_Extender #(.in_width(32), .out_width(5)) bit_extender_1 (.in(ALU_Y), .out(bit_extender_1_out));
  Bit_Extender #(.in_width(32), .out_width(5)) bit_extender_2 (.in(ALU_Y), .out(bit_extender_2_out));
  Bit_Extender #(.in_width(32), .out_width(5)) bit_extender_3 (.in(ALU_Y), .out(bit_extender_3_out));
  u_shift_left u_shift_left_1 (.in_1(ALU_X), .in_2(bit_extender_1_out), .out_3(LEFT_SHIFT_OUTPUT));
  Shifter #(.width(32), .shift("ar")) shifter_1 (.in(ALU_X), .\dist (bit_extender_2_out), .out(RIGHT_SHIFT_OUTPUT));
  assign AND_OUTPUT = ALU_X & ALU_Y;  // AND_Gate and_1, 32 bits wide
  assign OR_OUTPUT = ALU_X | ALU_Y;  // OR_Gate or_1, 32 bits wide
  u_REV u_rev_1 (.INPUT(ALU_X), .REVERSE_AMOUNT(bit_extender_3_out), .OUTPUT(REVER_OUTPUT));
  assign XOR_OUTPUT = ALU_X ^ ALU_Y;  // XOR_Gate xor_1, 32 bits wide
  Negator #(.width(32)) negator_1 (.in(ALU_Y), .out(negator_1_out));
  Adder #(.width(32)) adder_1 (.a(ALU_X), .b(ALU_Y), .out(ADD_OUTPUT));  // open: cin, cout
  Adder #(.width(32)) adder_2 (.a(ALU_X), .b(negator_1_out), .out(SUB_OUTPUT));  // open: cin, cout
  Multiplier #(.width(32)) multiplier_1 (.a(ALU_X), .b(ALU_Y), .out(MUL_OUTPUT));  // open: cin, cout
  u_division u_division_1 (.ALU_X(ALU_X), .ALU_Y(ALU_Y), .out_3(DIV_OUTPUT));  // open: out_4
  Adder #(.width(32)) adder_3 (.a(ALU_X), .b(ALU_Y), .out(RL_S));  // open: cin, cout
  Multiplexer #(.select(4), .width(32)) multiplexer_1 (
    .in0(LEFT_SHIFT_OUTPUT), .in1(RIGHT_SHIFT_OUTPUT), .in2(AND_OUTPUT), .in3(OR_OUTPUT), .in4(REVER_OUTPUT),
    .in5(XOR_OUTPUT), .in6(ADD_OUTPUT), .in7(SUB_OUTPUT), .in8(MUL_OUTPUT), .in9(DIV_OUTPUT), .in10(RL_S),
    .in11(RL_S), .in12(RL_S), .in13(RL_S), .in14({ALU_Y[16:0], ALU_X[14:0]}), .in15(ALU_Y), .out(ALU_RESULT),
    .sel(ALU_CONTROL));  // open: en

  // Other names for the same wires on the sheet: SET_UPPER_OUTPUT[31:0] = {ALU_Y[16:0], ALU_X[14:0]}; X[31:0] = ALU_X;
  //   J[31:0] = ALU_Y; Y[31:0] = ALU_Y
endmodule

// Data Memory
module u_MEM (
  input  [24:0] ADDRESS,
  input  WORD_MODE,
  input  MEM_WRITE,
  input  [31:0] DATA_IN,
  input  CLOCK,
  output [31:0] DATA_OUT
);

  wire not_1_out, not_2_out;
  wire [0:0] adder_1_out;
  wire [15:0] data0, data1, even, multiplexer_2_out, multiplexer_4_out, multiplexer_9_out, odd;
  wire [23:0] add0, add1, evenadd, multiplexer_1_out, multiplexer_3_out, oddadd, plus_1;
  wire [31:0] bit_extender_1_out, multiplexer_10_out;

  Adder #(.width(25)) adder_1 (.a(ADDRESS), .b(25'h1), .out({plus_1, adder_1_out[0]}));  // open: cin, cout
  Demultiplexer #(.width(24)) demultiplexer_1 (
    .out0(evenadd), .out1(oddadd), .in(ADDRESS[24:1]), .sel(ADDRESS[0]));  // open: en
  Multiplexer #(.width(24)) multiplexer_1 (
    .in0(evenadd), .in1(plus_1), .out(multiplexer_1_out), .sel(ADDRESS[0]));  // open: en
  Multiplexer #(.width(16)) multiplexer_2 (
    .in0(DATA_IN[15:0]), .in1(DATA_IN[31:16]), .out(multiplexer_2_out), .sel(ADDRESS[0]));  // open: en
  Multiplexer #(.width(24)) multiplexer_3 (
    .in0(plus_1), .in1(oddadd), .out(multiplexer_3_out), .sel(ADDRESS[0]));  // open: en
  Multiplexer #(.width(16)) multiplexer_4 (
    .in0(DATA_IN[31:16]), .in1(DATA_IN[15:0]), .out(multiplexer_4_out), .sel(ADDRESS[0]));  // open: en
  not not_1 (not_1_out, MEM_WRITE);
  not not_2 (not_2_out, MEM_WRITE);
  RAM #(.addrWidth(24), .dataWidth(16), .bus("separate")) ram_1 (
    .addr(add0), .din(data0), .data(even), .str(MEM_WRITE), .clk(CLOCK), .ld(not_1_out));  // open: sel, clr
  RAM #(.addrWidth(24), .dataWidth(16), .bus("separate")) ram_2 (
    .addr(add1), .din(data1), .data(odd), .str(MEM_WRITE), .clk(CLOCK), .ld(not_2_out));  // open: sel, clr
  Multiplexer #(.width(24)) multiplexer_5 (
    .in0(evenadd), .in1(multiplexer_1_out), .out(add0), .sel(WORD_MODE));  // open: en
  Multiplexer #(.width(16)) multiplexer_6 (
    .in0(DATA_IN[15:0]), .in1(multiplexer_2_out), .out(data0), .sel(WORD_MODE));  // open: en
  Multiplexer #(.width(24)) multiplexer_7 (
    .in0(oddadd), .in1(multiplexer_3_out), .out(add1), .sel(WORD_MODE));  // open: en
  Multiplexer #(.width(16)) multiplexer_8 (
    .in0(DATA_IN[15:0]), .in1(multiplexer_4_out), .out(data1), .sel(WORD_MODE));  // open: en
  Multiplexer #(.width(16)) multiplexer_9 (
    .in0(even), .in1(odd), .out(multiplexer_9_out), .sel(ADDRESS[0]));  // open: en
  assign bit_extender_1_out = {{16{multiplexer_9_out[15]}}, multiplexer_9_out};  // Bit_Extender bit_extender_1
  Multiplexer #(.width(32)) multiplexer_10 (
    .in0({odd, even}), .in1({even, odd}), .out(multiplexer_10_out), .sel(ADDRESS[0]));  // open: en
  // Probe on multiplexer_10_out
  // Probe on bit_extender_1_out
  Multiplexer #(.width(32)) multiplexer_11 (
    .in0(bit_extender_1_out), .in1(multiplexer_10_out), .out(DATA_OUT), .sel(WORD_MODE));  // open: en

  // Other names for the same wires on the sheet: oe = ADDRESS[0]; clk = CLOCK; DATA[31:0] = DATA_IN;
  //   lower[15:0] = DATA_IN[15:0]; upper[15:0] = DATA_IN[31:16]; en = MEM_WRITE; mode = WORD_MODE;
  //   result[31:0] = DATA_OUT
endmodule

module u_REV (
  input  [31:0] INPUT,
  input  [4:0] REVERSE_AMOUNT,
  output [31:0] OUTPUT
);

  wire [1:0] _0200, _0201, _0202, _0203, _0204, _0205, _0206, _0207, _0208, _0209, _0210, _0211, _0212,
       _0213, _0214, _0215;
  wire [3:0] _0300, _0301, _0302, _0303, _0304, _0305, _0306, _0307;
  wire [7:0] _0400, _0401, _0402, _0403;
  wire [31:0] multiplexer_4_out;

  // Probe on INPUT
  // Probe on {_0215, _0214, _0213, _0212, _0211, _0210, _0209, _0208, _0207, _0206, _0205, _0204, _0203, _0202, _0201, _0200}
  Multiplexer #(.width(32)) multiplexer_1 (
    .in0(INPUT),
    .in1({INPUT[30], INPUT[31], INPUT[28], INPUT[29], INPUT[26], INPUT[27], INPUT[24], INPUT[25], INPUT[22], INPUT[23], INPUT[20], INPUT[21], INPUT[18], INPUT[19], INPUT[16], INPUT[17], INPUT[14], INPUT[15], INPUT[12], INPUT[13], INPUT[10], INPUT[11], INPUT[8], INPUT[9], INPUT[6], INPUT[7], INPUT[4], INPUT[5], INPUT[2], INPUT[3], INPUT[0], INPUT[1]}),
    .out({_0215, _0214, _0213, _0212, _0211, _0210, _0209, _0208, _0207, _0206, _0205, _0204, _0203, _0202, _0201, _0200}),
    .sel(REVERSE_AMOUNT[0]));  // open: en
  Multiplexer #(.width(32)) multiplexer_2 (
    .in0({_0215, _0214, _0213, _0212, _0211, _0210, _0209, _0208, _0207, _0206, _0205, _0204, _0203, _0202, _0201, _0200}),
    .in1({_0214, _0215, _0212, _0213, _0210, _0211, _0208, _0209, _0206, _0207, _0204, _0205, _0202, _0203, _0200, _0201}),
    .out({_0307, _0306, _0305, _0304, _0303, _0302, _0301, _0300}), .sel(REVERSE_AMOUNT[1]));  // open: en
  // Probe on {_0307, _0306, _0305, _0304, _0303, _0302, _0301, _0300}
  Multiplexer #(.width(32)) multiplexer_3 (
    .in0({_0307, _0306, _0305, _0304, _0303, _0302, _0301, _0300}),
    .in1({_0306, _0307, _0304, _0305, _0302, _0303, _0300, _0301}), .out({_0403, _0402, _0401, _0400}),
    .sel(REVERSE_AMOUNT[2]));  // open: en
  // Probe on {_0403, _0402, _0401, _0400}
  Multiplexer #(.width(32)) multiplexer_4 (
    .in0({_0403, _0402, _0401, _0400}), .in1({_0402, _0403, _0400, _0401}), .out(multiplexer_4_out),
    .sel(REVERSE_AMOUNT[3]));  // open: en
  // Probe on multiplexer_4_out
  Multiplexer #(.width(32)) multiplexer_5 (
    .in0(multiplexer_4_out), .in1({multiplexer_4_out[15:0], multiplexer_4_out[31:16]}), .out(OUTPUT),
    .sel(REVERSE_AMOUNT[4]));  // open: en
  // Probe on OUTPUT

  // Other names for the same wires on the sheet: _0101 = INPUT[1]; _0100 = INPUT[0]; _0103 = INPUT[3];
  //   _0102 = INPUT[2]; _0105 = INPUT[5]; _0104 = INPUT[4]; _0107 = INPUT[7]; _0106 = INPUT[6]; _0109 = INPUT[9];
  //   _0108 = INPUT[8]; _0111 = INPUT[11]; _0110 = INPUT[10]; _0113 = INPUT[13]; _0112 = INPUT[12]; _0115 = INPUT[15];
  //   _0114 = INPUT[14]; _0117 = INPUT[17]; _0116 = INPUT[16]; _0119 = INPUT[19]; _0118 = INPUT[18];
  //   _0121 = INPUT[21]; _0120 = INPUT[20]; _0123 = INPUT[23]; _0122 = INPUT[22]; _0125 = INPUT[25];
  //   _0124 = INPUT[24]; _0127 = INPUT[27]; _0126 = INPUT[26]; _0129 = INPUT[29]; _0128 = INPUT[28];
  //   _0131 = INPUT[31]; _0130 = INPUT[30]; bit0 = REVERSE_AMOUNT[0]; bit1 = REVERSE_AMOUNT[1];
  //   bit2 = REVERSE_AMOUNT[2]; bit3 = REVERSE_AMOUNT[3]; bit4 = REVERSE_AMOUNT[4]

  // Notes on the sheet:
  //   Feel free to use this component, or not, however you want!
endmodule

module u_shift_left (
  input  [31:0] in_1,
  input  [4:0] in_2,
  output [31:0] out_3
);

  wire LSB;
  wire [31:0] fifth, first, fourth, or_1_out, or_2_out, or_4_out, or_5_out, or_6_out, \output , second,
       shifter_1_out, shifter_2_out, shifter_3_out, shifter_4_out, shifter_5_out, shifter_6_out, third;

  Shifter #(.width(32)) shifter_1 (.in(in_1), .\dist (5'b00001), .out(shifter_1_out));
  assign or_1_out = shifter_1_out | 32'h1;  // OR_Gate or_1, 32 bits wide
  Shifter #(.width(32)) shifter_2 (.in(first), .\dist (5'b00010), .out(shifter_2_out));
  Shifter #(.width(32)) shifter_3 (.in(in_1), .\dist (in_2), .out(shifter_3_out));
  Multiplexer #(.width(32)) multiplexer_1 (.in0(in_1), .in1(or_1_out), .out(first), .sel(in_2[0]));  // open: en
  assign or_2_out = shifter_2_out | 32'h3;  // OR_Gate or_2, 32 bits wide
  Multiplexer #(.width(32)) multiplexer_2 (.in0(first), .in1(or_2_out), .out(second), .sel(in_2[1]));  // open: en
  assign \output  = shifter_3_out | fifth;  // OR_Gate or_3, 32 bits wide
  Shifter #(.width(32)) shifter_4 (.in(second), .\dist (5'b00100), .out(shifter_4_out));
  Bit_Extender #(.in_width(32), .out_width(1)) bit_extender_1 (.in(in_1), .out(LSB));
  assign or_4_out = shifter_4_out | 32'hf;  // OR_Gate or_4, 32 bits wide
  Multiplexer #(.width(32)) multiplexer_3 (.in0(second), .in1(or_4_out), .out(third), .sel(in_2[2]));  // open: en
  Shifter #(.width(32)) shifter_5 (.in(third), .\dist (5'b01000), .out(shifter_5_out));
  assign or_5_out = shifter_5_out | 32'hff;  // OR_Gate or_5, 32 bits wide
  Multiplexer #(.width(32)) multiplexer_4 (.in0(third), .in1(or_5_out), .out(fourth), .sel(in_2[3]));  // open: en
  Shifter #(.width(32)) shifter_6 (.in(fourth), .\dist (5'b10000), .out(shifter_6_out));
  Multiplexer #(.width(32)) multiplexer_5 (.in0(fourth), .in1(or_6_out), .out(fifth), .sel(in_2[4]));  // open: en
  assign or_6_out = shifter_6_out | 32'hffff;  // OR_Gate or_6, 32 bits wide
  Multiplexer #(.width(32)) multiplexer_6 (.in0(shifter_3_out), .in1(\output ), .out(out_3), .sel(LSB));  // open: en

  // Other names for the same wires on the sheet: final[31:0] = out_3; input[31:0] = in_1
endmodule

module u_division (
  input  [31:0] ALU_X,
  input  [31:0] ALU_Y,
  output [31:0] out_3,
  output [31:0] out_4
);

  wire comparator_1_gt, comparator_2_eq, comparator_3_lt, comparator_5_lt, comparator_6_eq, comparator_7_eq,
       OUTPUT, OUTPUT1, sign, zero;
  wire [30:0] absResult, adder_1_out, adder_2_out, adder_3_out, divResult, not_1_out, not_2_out, not_3_out,
       valx, valy;
  wire [31:0] bit_extender_1_out, bit_extender_2_out, multiplexer_3_out, negative_zero, positive_zero;

  // Probe on ALU_Y
  assign bit_extender_1_out = {{31{1'b0}}, OUTPUT1};  // Bit_Extender bit_extender_1
  assign not_1_out = ~ALU_X[30:0];  // NOT_Gate not_1, 31 bits wide
  assign bit_extender_2_out = {{31{1'b0}}, OUTPUT};  // Bit_Extender bit_extender_2
  Shifter #(.width(32)) shifter_1 (.in(bit_extender_1_out), .\dist ({5{1'b1}}), .out(negative_zero));
  Adder #(.width(31)) adder_1 (.a(not_1_out), .b(31'h1), .out(adder_1_out));  // open: cin, cout
  assign not_2_out = ~ALU_Y[30:0];  // NOT_Gate not_2, 31 bits wide
  Adder #(.width(31)) adder_2 (.a(not_2_out), .b(31'h1), .out(adder_2_out));  // open: cin, cout
  Comparator #(.width(32)) comparator_1 (.a(ALU_X), .b({32{1'b0}}), .gt(comparator_1_gt));  // open: eq, lt
  Comparator #(.width(32)) comparator_2 (.a(ALU_Y), .b({32{1'b0}}), .eq(comparator_2_eq));  // open: gt, lt
  u_shift_left u_shift_left_1 (.in_1(bit_extender_2_out), .in_2(5'b11110), .out_3(positive_zero));
  Multiplexer #(.width(31)) multiplexer_1 (
    .in0(ALU_X[30:0]), .in1(adder_1_out), .out(valx), .sel(ALU_X[31]));  // open: en
  Multiplexer #(.width(31)) multiplexer_2 (
    .in0(ALU_Y[30:0]), .in1(adder_2_out), .out(valy), .sel(ALU_Y[31]));  // open: en
  and and_1 (OUTPUT, comparator_1_gt, comparator_2_eq);
  Divider #(.width(31)) divider_1 (.a(valx), .b(valy), .out(divResult));  // open: upper, rem
  Comparator #(.width(32)) comparator_3 (.a(ALU_X), .b({32{1'b0}}), .lt(comparator_3_lt));  // open: gt, eq
  Multiplexer #(.width(32)) multiplexer_3 (
    .in0(positive_zero), .in1(negative_zero), .out(multiplexer_3_out), .sel(comparator_3_lt));  // open: en
  Comparator #(.width(32)) comparator_4 (.a(ALU_X), .b({32{1'b0}}), .eq(zero));  // open: gt, lt
  Comparator #(.width(32)) comparator_5 (.a(ALU_X), .b({32{1'b0}}), .lt(comparator_5_lt));  // open: gt, eq
  Comparator #(.width(32)) comparator_6 (.a(ALU_Y), .b({32{1'b0}}), .eq(comparator_6_eq));  // open: gt, lt
  Multiplexer #(.width(32)) multiplexer_4 (
    .in0(out_4), .in1(multiplexer_3_out), .out(out_3), .sel(comparator_7_eq));  // open: en
  and and_2 (OUTPUT1, comparator_5_lt, comparator_6_eq);
  Comparator #(.width(32)) comparator_7 (.a(ALU_Y), .b({32{1'b0}}), .eq(comparator_7_eq));  // open: gt, lt
  xor xor_1 (sign, ALU_X[31], ALU_Y[31]);
  assign not_3_out = ~divResult;  // NOT_Gate not_3, 31 bits wide
  Multiplexer #(.width(32)) multiplexer_5 (
    .in0({sign, absResult}), .in1({32{1'b0}}), .out(out_4), .sel(zero));  // open: en
  Multiplexer #(.width(31)) multiplexer_6 (
    .in0(divResult), .in1(adder_3_out), .out(absResult), .sel(sign));  // open: en
  Adder #(.width(31)) adder_3 (.a(not_3_out), .b(31'h1), .out(adder_3_out));  // open: cin, cout

  // Other names for the same wires on the sheet: div_solution[31:0] = out_3; normal_div[31:0] = out_4;
  //   unvalx[30:0] = ALU_X[30:0]; X[31:0] = ALU_X; signX = ALU_X[31]; unvaly[30:0] = ALU_Y[30:0]; Y[31:0] = ALU_Y;
  //   signY = ALU_Y[31]
endmodule
